// Digital circuit control.dig as structural Verilog
module control (
  input  [15:0] Instr,
  input  En,
  output [3:0] RT,
  output RTW,
  output [3:0] RA,
  output [3:0] AluOp,
  output AluD,
  output [7:0] Imm,
  output LoD,
  output HiD,
  output Jmp,
  output [3:0] JT,
  output Halt,
  output JReg,
  output RReg,
  output MemD,
  output RTD,
  output WMem
);

  wire _0_3RA, _0_7Imm, _4_7RT, _4_15AllHigh, _4RReg, _8_11AluOp, _8_11Imm, _8_11JT, _8_11RT, and_13_out,
       and_14_out, and_15_out, decoder_1_out_0, decoder_1_out_4, decoder_1_out_8, Halt_t, HiD_t, Jmp_t,
       LoD_t, MemD_t, RReg_t, RTD_t, RTW_t;
  wire [3:0] AluOp_t, JT_t, RA_t, RT_t;
  wire [7:0] Imm_t;

  assign JT_t = _8_11JT ? Instr[11:8] : 4'bz;  // Driver driver_1
  assign AluOp_t = _8_11AluOp ? Instr[11:8] : 4'bz;  // Driver driver_2
  assign RT_t = _8_11RT ? Instr[11:8] : 4'bz;  // Driver driver_3
  assign Imm_t = _8_11Imm ? {4'b0000, Instr[11:8]} : 8'bz;  // Driver driver_4
  assign RT_t = _4_7RT ? Instr[7:4] : 4'bz;  // Driver driver_5
  assign RReg_t = _4RReg ? Instr[4] : 1'bz;  // Driver driver_6
  Decoder #(.Selector_Bits(4)) decoder_1 (
    .sel(Instr[15:12]), .out_0(decoder_1_out_0), .out_1(_8_11AluOp), .out_2(LoD_t), .out_3(HiD_t),
    .out_4(decoder_1_out_4), .out_5(_4RReg), .out_6(MemD_t), .out_7(RTD_t), .out_8(decoder_1_out_8));  // open: out_9, out_10, out_11, out_12, out_13, out_14, out_15
  or or_1 (_8_11RT, LoD_t, HiD_t);
  or or_2 (_4_7RT, _8_11AluOp, MemD_t, RTD_t);
  or or_3 (RTW_t, _8_11AluOp, LoD_t, HiD_t, MemD_t);
  or or_4 (_0_3RA, _8_11AluOp, _4RReg, MemD_t, RTD_t);
  or or_5 (_0_7Imm, LoD_t, HiD_t, decoder_1_out_4);
  or or_6 (Jmp_t, decoder_1_out_4, _4RReg);
  or or_7 (_8_11JT, decoder_1_out_4, _4RReg);
  and and_1 (Halt_t, decoder_1_out_0, _4_15AllHigh);
  or or_8 (_8_11Imm, MemD_t, RTD_t);
  assign Imm_t = _0_7Imm ? Instr[7:0] : 8'bz;  // Driver driver_7
  assign RA_t = _0_3RA ? Instr[3:0] : 4'bz;  // Driver driver_8
  assign RT = En ? RT_t : 4'bz;  // Driver driver_9
  and and_2 (RTW, RTW_t, En);
  assign RA = En ? RA_t : 4'bz;  // Driver driver_10
  assign AluOp = En ? AluOp_t : 4'bz;  // Driver driver_11
  and and_3 (AluD, _8_11AluOp, En);
  assign Imm = En ? Imm_t : 8'bz;  // Driver driver_12
  and and_4 (LoD, LoD_t, En);
  and and_5 (HiD, HiD_t, En);
  and and_6 (Jmp, Jmp_t, En);
  assign JT = En ? JT_t : 4'bz;  // Driver driver_13
  and and_7 (Halt, Halt_t, En);
  and and_8 (JReg, _4RReg, En);
  and and_9 (RReg, RReg_t, En);
  and and_10 (MemD, MemD_t, En);
  and and_11 (RTD, RTD_t, En);
  and and_12 (WMem, RTD_t, En);
  and and_13 (and_13_out, Instr[11], Instr[10]);
  and and_14 (and_14_out, Instr[9], Instr[8], Instr[7], Instr[6], Instr[5]);
  and and_15 (and_15_out, Instr[4], Instr[3], Instr[2], Instr[1], Instr[0]);
  and and_16 (_4_15AllHigh, and_13_out, and_14_out, and_15_out);

  // Other names for the same wires on the sheet: AluD_t = _8_11AluOp; JReg_t = _4RReg; WMem_t = RTD_t

  // Notes on the sheet:
  //   RT: Address of target register
  //   RTW: Address of target register
  //   RA: Address of argument register
  //   AluOp: ALU operation to perform
  //   En: Enabled when on
  //   AluD: High when ALU result should be sent to data bus
  //   Imm: 8 bit immediate value
  //   LoD: Write target with low bits set to Imm to data
  //   HiD: Write target with high bits set to Imm to data
  //   Jmp: When high, jump if jump decider is true
  //   JT: Four bit jump type
  //   Halt: When high, write jump location to data bus
  //   JReg: Jump using register based jump
  //   RReg: When jumping with a register, use it as a relative value
  //   MemD: When high, write memroy data to the data bus
  //   RTD: When high, write target register data to the data bus
  //   WMem: When high, write data from the data bus to memory
endmodule
