// Digital circuit hardware.dig as structural Verilog
module hardware (
  input  clk,
  input  in_2,
  input  in_3
);

  wire AluD, and_1_out, and_2_out, control_1_p14, control_1_p15, Halt, HiD, Jmp, jumpdecider_1_jmp, LoD,
       MemD, not_1_out, Phase_out, rs_ff_1_nq, rs_ff_1_q, RTD, RTW, Un_Halt_out;
  wire [3:0] alu_1_fl, AluOp, Flags_q, JT, RA, RT;
  wire [7:0] registerfile_1_da, registerfile_1_da_2;
  wire [15:0] add_1_s, alu_1_rdata, driver_1_out, InstrReg_q, jumpcalc_1_npc, multiplexer_1_out, PC_out,
       ramdualport_1_d, registerfile_1_db;
  wire [15:8] control_1_p8;

  Button Un_Halt (.out(Un_Halt_out));
  RS_FF rs_ff_1 (.S(Halt), .C(clk), .R(Un_Halt_out), .Q(rs_ff_1_q), .nQ(rs_ff_1_nq));
  and and_1 (and_1_out, rs_ff_1_nq, clk);
  LED Halted (.in(rs_ff_1_q));
  LED Running (.in(and_1_out));
  Counter Phase (.en(1'b1), .C(and_1_out), .clr(1'b0), .out(Phase_out));  // open: ovf
  not not_1 (not_1_out, Phase_out);
  CounterPreset #(.Bits(16)) PC (
    .en(not_1_out), .C(and_1_out), .dir(in_2), .in(jumpcalc_1_npc), .ld(and_2_out), .clr(in_3), .out(PC_out));  // open: ovf
  Multiplexer #(.Bits(16)) multiplexer_1 (.sel(Phase_out), .in_0(PC_out), .in_1(add_1_s), .out(multiplexer_1_out));
  RAMDualPort #(.AddrBits(16), .isProgramMemory("true"), .Bits(16)) ramdualport_1 (
    .A(multiplexer_1_out), .Din(driver_1_out), .str(RTD), .C(and_1_out), .ld(1'b1), .D(ramdualport_1_d));
  assign driver_1_out = MemD ? ramdualport_1_d : 16'bz;  // Driver driver_1
  Register #(.Bits(16)) InstrReg (.D(ramdualport_1_d), .C(and_1_out), .en(not_1_out), .Q(InstrReg_q));
  RegisterFile #(.AddrBits(4), .Bits(16)) registerfile_1 (
    .Din(driver_1_out), .we(RTW), .Rw(RT), .C(and_1_out), .Ra(RT), .Rb(RA),
    .Da({registerfile_1_da_2, registerfile_1_da}), .Db(registerfile_1_db));
  // Probe on InstrReg_q
  Add #(.Bits(16)) add_1 (.a(registerfile_1_db), .b({{8{1'b0}}, control_1_p8}), .c_i(1'b0), .s(add_1_s));  // open: c_o
  assign driver_1_out = RTD ? {registerfile_1_da_2, registerfile_1_da} : 16'bz;  // Driver driver_2
  // control control_1: pin names not known; wires that end beside it: InstrReg_q, Phase_out, RT, RTW, RA, AluOp, AluD, control_1_p8, LoD, HiD, Jmp, JT, Halt, control_1_p14, control_1_p15, MemD, RTD
  alu alu_1 (
    .Op(AluOp), .TData({registerfile_1_da_2, registerfile_1_da}), .AData(registerfile_1_db),
    .RData(alu_1_rdata), .Fl(alu_1_fl));
  assign driver_1_out = AluD ? alu_1_rdata : 16'bz;  // Driver driver_3
  Register #(.Bits(4)) Flags (.D(alu_1_fl), .C(and_1_out), .en(AluD), .Q(Flags_q));
  // Probe on control_1_p8
  jumpCalc jumpcalc_1 (
    .PC(PC_out), .Imm(control_1_p8), .Reg(registerfile_1_db), .JReg(control_1_p14), .RRel(control_1_p15),
    .nPC(jumpcalc_1_npc));
  assign driver_1_out = LoD ? {registerfile_1_da_2, control_1_p8} : 16'bz;  // Driver driver_4
  assign driver_1_out = HiD ? {control_1_p8, registerfile_1_da} : 16'bz;  // Driver driver_5
  and and_2 (and_2_out, Jmp, jumpdecider_1_jmp);
  jumpDecider jumpdecider_1 (.JT(JT), .Fl(Flags_q), .Jmp(jumpdecider_1_jmp));
  LED led_1 (.in(Flags_q[0]));
  LED led_2 (.in(Flags_q[1]));
  LED led_3 (.in(Flags_q[2]));
  LED led_4 (.in(Flags_q[3]));
  // Probe on PC_out
  // Probe on driver_1_out

  // Notes on the sheet:
  //   clk: Hz: 20
  //   Imm
  //   fN
  //   fZ
  //   fC
  //   fO
  //   PC
  //   Data
endmodule
